// Logisim project lab1_part2_simplified.circ as structural Verilog: 1 circuit, main circuit main
module main (
  input  a,
  input  c,
  input  b,
  output f
);

  wire not_1_out, not_2_out, or_1_out;

  not not_1 (not_1_out, a);
  not not_2 (not_2_out, b);
  or or_1 (or_1_out, not_1_out, c);
  and and_1 (f, or_1_out, not_2_out);
endmodule
