// Logisim project Lab2_Part2.circ as structural Verilog: 3 circuits, main circuit main
module main (
  input  SW_9,
  input  SW_0,
  input  SW_1,
  input  SW_8,
  input  SW_2,
  input  SW_3,
  output LEDR_0
);

  mux4to1 mux4to1_1 (.s1(SW_9), .u(SW_0), .v(SW_1), .s0(SW_8), .w(SW_2), .x(SW_3), .m(LEDR_0));
endmodule

module mux2to1 (
  input  x,
  input  y,
  input  s,
  output m
);

  Multiplexer #(.enable("false")) multiplexer_1 (.in0(x), .in1(y), .out(m), .sel(s));
endmodule

module mux4to1 (
  input  s1,
  input  u,
  input  v,
  input  s0,
  input  w,
  input  x,
  output m
);

  wire mux2to1_1_m, mux2to1_3_m;

  mux2to1 mux2to1_1 (.x(u), .y(v), .s(s0), .m(mux2to1_1_m));
  mux2to1 mux2to1_3 (.x(w), .y(x), .s(s0), .m(mux2to1_3_m));
  mux2to1 mux2to1_2 (.x(mux2to1_1_m), .y(mux2to1_3_m), .s(s1), .m(m));
endmodule
