// Logisim project Lab2_Part3.circ as structural Verilog: 9 circuits, main circuit m_total
module m_total (
  input  c3,
  input  c2,
  input  c1,
  input  c0,
  output HEX0,
  output HEX1,
  output HEX2,
  output HEX3,
  output HEX4,
  output HEX5,
  output HEX6
);

  M0 M0_1 (.c0(c0), .c1(c1), .c2(c2), .c3(c3), .HEX0(HEX0));
  M1 M1_1 (.c3(c3), .c2(c2), .c1(c1), .c0(c0), .HEX1(HEX1));
  M2 M2_1 (.c3(c3), .c2(c2), .c1(c1), .c0(c0), .HEX2(HEX2));
  M3 M3_1 (.c3(c3), .c2(c2), .c1(c1), .c0(c0), .HEX3(HEX3));
  M4 M4_1 (.c3(c3), .c2(c2), .c1(c1), .c0(c0), .HEX4(HEX4));
  M5 M5_1 (.c3(c3), .c2(c2), .c1(c1), .c0(c0), .HEX5(HEX5));
  M6 M6_1 (.c3(c3), .c2(c2), .c1(c1), .c0(c0), .HEX6(HEX6));
endmodule

module M0 (
  input  c0,
  input  c1,
  input  c2,
  input  c3,
  output HEX0
);

  wire and_1_out, and_2_out, and_3_out, and_4_out, not_1_out, not_2_out, not_3_out, not_4_out, not_5_out;

  not not_1 (not_1_out, c1);
  not not_2 (not_2_out, c2);
  not not_3 (not_3_out, c3);
  not not_4 (not_4_out, c0);
  and and_1 (and_1_out, not_4_out, not_1_out, c2, not_3_out);
  not not_5 (not_5_out, c2);
  and and_2 (and_2_out, not_3_out, not_5_out, not_1_out, c0);
  and and_3 (and_3_out, c0, not_1_out, c2, c3);
  and and_4 (and_4_out, c0, c1, not_2_out, c3);
  or or_1 (HEX0, and_1_out, and_2_out, and_3_out, and_4_out);
endmodule

module M1 (
  input  c3,
  input  c2,
  input  c1,
  input  c0,
  output HEX1
);

  wire and_1_out, and_2_out, and_3_out, and_4_out, not_1_out, not_2_out, not_3_out;

  not not_1 (not_1_out, c3);
  not not_2 (not_2_out, c1);
  not not_3 (not_3_out, c0);
  and and_1 (and_1_out, not_1_out, c2, not_2_out, c0);
  and and_2 (and_2_out, c3, c2, not_3_out);
  and and_3 (and_3_out, c3, c1, c0);
  and and_4 (and_4_out, c2, c1, not_3_out);
  or or_1 (HEX1, and_1_out, and_4_out, and_2_out, and_3_out);
endmodule

module M2 (
  input  c3,
  input  c2,
  input  c1,
  input  c0,
  output HEX2
);

  wire and_1_out, and_2_out, and_3_out, not_1_out, not_2_out, not_3_out;

  not not_1 (not_1_out, c3);
  not not_2 (not_2_out, c2);
  not not_3 (not_3_out, c0);
  and and_1 (and_1_out, not_1_out, not_2_out, c1, not_3_out);
  and and_2 (and_2_out, c3, c2, not_3_out);
  and and_3 (and_3_out, c3, c2, c1);
  or or_1 (HEX2, and_1_out, and_3_out, and_2_out);
endmodule

module M3 (
  input  c3,
  input  c2,
  input  c1,
  input  c0,
  output HEX3
);

  wire and_1_out, and_2_out, and_3_out, and_4_out, not_1_out, not_2_out, not_3_out, not_4_out;

  not not_1 (not_1_out, c2);
  not not_2 (not_2_out, c3);
  not not_3 (not_3_out, c1);
  not not_4 (not_4_out, c0);
  and and_1 (and_1_out, not_2_out, c2, not_3_out, not_4_out);
  and and_2 (and_2_out, not_1_out, not_3_out, c0);
  and and_3 (and_3_out, c2, c1, c0);
  and and_4 (and_4_out, c3, not_1_out, c1, not_4_out);
  or or_1 (HEX3, and_1_out, and_4_out, and_2_out, and_3_out);
endmodule

module M4 (
  input  c3,
  input  c2,
  input  c1,
  input  c0,
  output HEX4
);

  wire and_1_out, and_2_out, and_3_out, not_1_out, not_2_out, not_3_out;

  not not_1 (not_1_out, c2);
  not not_2 (not_2_out, c3);
  not not_3 (not_3_out, c1);
  and and_1 (and_1_out, not_2_out, c2, not_3_out);
  and and_2 (and_2_out, not_2_out, c0);
  and and_3 (and_3_out, not_1_out, not_3_out, c0);
  or or_1 (HEX4, and_1_out, and_2_out, and_3_out);
endmodule

module M5 (
  input  c3,
  input  c2,
  input  c1,
  input  c0,
  output HEX5
);

  wire and_1_out, and_2_out, and_3_out, and_4_out, not_1_out, not_2_out, not_3_out;

  not not_1 (not_1_out, c3);
  not not_2 (not_2_out, c2);
  not not_3 (not_3_out, c1);
  and and_1 (and_1_out, c3, c2, not_3_out, c0);
  and and_2 (and_2_out, not_1_out, not_2_out, c0);
  and and_3 (and_3_out, not_1_out, c1, c0);
  and and_4 (and_4_out, not_1_out, not_2_out, c1);
  or or_1 (HEX5, and_1_out, and_2_out, and_3_out, and_4_out);
endmodule

module M6 (
  input  c3,
  input  c2,
  input  c1,
  input  c0,
  output HEX6
);

  wire and_1_out, and_2_out, and_3_out, not_1_out, not_2_out, not_3_out, not_4_out;

  not not_1 (not_1_out, c3);
  not not_2 (not_2_out, c2);
  not not_3 (not_3_out, c1);
  not not_4 (not_4_out, c0);
  and and_1 (and_1_out, not_1_out, not_2_out, not_3_out);
  and and_2 (and_2_out, c3, c2, not_3_out, not_4_out);
  and and_3 (and_3_out, c0, c1, c2, not_1_out);
  or or_1 (HEX6, and_1_out, and_2_out, and_3_out);
endmodule

module main (
  input  SW_3,
  input  SW_2,
  input  SW_1,
  input  SW_0
);

  wire m_total_1_hex0, m_total_1_hex1, m_total_1_hex2, m_total_1_hex3, m_total_1_hex4, m_total_1_hex5,
       m_total_1_hex6;

  m_total m_total_1 (
    .c3(SW_3), .c2(SW_2), .c1(SW_1), .c0(SW_0), .HEX0(m_total_1_hex0), .HEX1(m_total_1_hex1),
    .HEX2(m_total_1_hex2), .HEX3(m_total_1_hex3), .HEX4(m_total_1_hex4), .HEX5(m_total_1_hex5),
    .HEX6(m_total_1_hex6));
  _7_Segment_Display #(.active("false")) L_7_Segment_Display_1 (
    .g(m_total_1_hex6), .f(m_total_1_hex5), .a(m_total_1_hex0), .b(m_total_1_hex1), .e(m_total_1_hex4),
    .d(m_total_1_hex3), .c(m_total_1_hex2));  // open: dp
endmodule
