// Logisim project lab3_part1.circ as structural Verilog: 1 circuit, main circuit main
module main (
  input  [9:0] SW,
  output LEDR_0
);

  Multiplexer #(.enable("false"), .select(3)) multiplexer_1 (
    .in0(SW[3]), .in1(SW[4]), .in2(SW[5]), .in3(SW[6]), .in4(SW[7]), .in5(SW[8]), .in6(SW[9]), .out(LEDR_0),
    .sel(SW[2:0]));  // open: in7
endmodule
