// Logisim project lab3_part2.circ as structural Verilog: 2 circuits, main circuit FA
module FA (
  input  c_in,
  input  B,
  input  A,
  output s,
  output c_out
);

  wire xor_1_out;

  xor xor_1 (xor_1_out, B, A);
  Multiplexer #(.enable("false")) multiplexer_1 (.in0(A), .in1(c_in), .out(c_out), .sel(xor_1_out));
  xor xor_2 (s, c_in, xor_1_out);
endmodule

module ripple_adder (
  input  c_in,
  input  [3:0] a,
  input  [3:0] b,
  output LEDR_1,
  output LEDR_2,
  output LEDR_0,
  output LEDR_3,
  output LEDR_4
);

  wire fa_2_c_out, fa_3_c_out, fa_4_c_out;

  FA fa_1 (.c_in(fa_2_c_out), .B(b[3]), .A(a[3]), .s(LEDR_3), .c_out(LEDR_4));
  FA fa_2 (.c_in(fa_3_c_out), .B(b[2]), .A(a[2]), .s(LEDR_2), .c_out(fa_2_c_out));
  FA fa_3 (.c_in(fa_4_c_out), .B(b[1]), .A(a[1]), .s(LEDR_1), .c_out(fa_3_c_out));
  FA fa_4 (.c_in(c_in), .B(b[0]), .A(a[0]), .s(LEDR_0), .c_out(fa_4_c_out));
endmodule
