// Logisim project lab4_part1.circ as structural Verilog: 2 circuits, main circuit DLatch
module DLatch (
  input  D,
  input  CLK,
  output Qa,
  output Qb
);

  wire nand_1_out, nand_2_out, not_1_out;

  not not_1 (not_1_out, D);
  nand nand_1 (nand_1_out, D, CLK);
  nand nand_2 (nand_2_out, CLK, not_1_out);
  nand nand_3 (Qa, nand_1_out, Qb);
  nand nand_4 (Qb, Qa, nand_2_out);
endmodule

module masterSlave (
  input  in_1,
  input  in_2,
  output out_3
);

  wire dlatch_1_qa, not_1_out;

  not not_1 (not_1_out, in_2);
  DLatch dlatch_1 (.D(in_1), .CLK(in_2), .Qa(dlatch_1_qa));  // open: Qb
  DLatch dlatch_2 (.D(dlatch_1_qa), .CLK(not_1_out), .Qa(out_3));  // open: Qb
endmodule
