// Logisim project lab4_part2.circ as structural Verilog: 24 circuits, main circuit lab3_main
module main (
  input  [3:0] A,
  input  [2:0] C,
  input  enable,
  input  clk,
  input  R,
  output [7:0] out_6,
  output [7:0] out_7
);

  wire m_total_1_hex0, m_total_1_hex1, m_total_1_hex2, m_total_1_hex3, m_total_1_hex4, m_total_1_hex5,
       m_total_1_hex6, m_total_2_hex0, m_total_2_hex1, m_total_2_hex2, m_total_2_hex3, m_total_2_hex4,
       m_total_2_hex5, m_total_2_hex6, m_total_3_hex0, m_total_3_hex1, m_total_3_hex2, m_total_3_hex3,
       m_total_3_hex4, m_total_3_hex5, m_total_3_hex6;

  ALU alu_1 (.A(A), .B(out_7[3:0]), .C(C), .S(out_6));
  Register register_1 (.D(out_6), .en(enable), .clk(clk), .Q(out_7), .clr(R));
  LED led_1 (.in(out_7[0]));
  LED led_2 (.in(out_7[1]));
  LED led_3 (.in(out_7[2]));
  LED led_4 (.in(out_7[3]));
  LED led_5 (.in(out_7[4]));
  LED led_6 (.in(out_7[5]));
  LED led_7 (.in(out_7[6]));
  LED led_8 (.in(out_7[7]));
  m_total m_total_1 (
    .c3(A[3]), .c2(A[2]), .c1(A[1]), .c0(A[0]), .HEX0(m_total_1_hex0), .HEX1(m_total_1_hex1),
    .HEX2(m_total_1_hex2), .HEX3(m_total_1_hex3), .HEX4(m_total_1_hex4), .HEX5(m_total_1_hex5),
    .HEX6(m_total_1_hex6));
  m_total m_total_2 (
    .c3(out_7[3]), .c2(out_7[2]), .c1(out_7[1]), .c0(out_7[0]), .HEX0(m_total_2_hex0), .HEX1(m_total_2_hex1),
    .HEX2(m_total_2_hex2), .HEX3(m_total_2_hex3), .HEX4(m_total_2_hex4), .HEX5(m_total_2_hex5),
    .HEX6(m_total_2_hex6));
  _7_Segment_Display #(.active("false")) u_7_segment_display_1 (
    .g(m_total_1_hex6), .f(m_total_1_hex5), .a(m_total_1_hex0), .b(m_total_1_hex1), .e(m_total_1_hex4),
    .d(m_total_1_hex3), .c(m_total_1_hex2));  // open: dp
  m_total m_total_3 (
    .c3(out_7[7]), .c2(out_7[6]), .c1(out_7[5]), .c0(out_7[4]), .HEX0(m_total_3_hex0), .HEX1(m_total_3_hex1),
    .HEX2(m_total_3_hex2), .HEX3(m_total_3_hex3), .HEX4(m_total_3_hex4), .HEX5(m_total_3_hex5),
    .HEX6(m_total_3_hex6));
  _7_Segment_Display #(.active("false")) u_7_segment_display_2 (
    .g(m_total_3_hex6), .f(m_total_3_hex5), .a(m_total_3_hex0), .b(m_total_3_hex1), .e(m_total_3_hex4),
    .d(m_total_3_hex3), .c(m_total_3_hex2));  // open: dp
  _7_Segment_Display #(.active("false")) u_7_segment_display_3 (
    .g(m_total_2_hex6), .f(m_total_2_hex5), .a(m_total_2_hex0), .b(m_total_2_hex1), .e(m_total_2_hex4),
    .d(m_total_2_hex3), .c(m_total_2_hex2));  // open: dp
endmodule

module lab3_main (
  input  [3:0] A,
  input  [3:0] B,
  input  [2:0] C,
  output [7:0] S
);

  wire m_total_1_hex0, m_total_1_hex1, m_total_1_hex2, m_total_1_hex3, m_total_1_hex4, m_total_1_hex5,
       m_total_1_hex6, m_total_2_hex0, m_total_2_hex1, m_total_2_hex2, m_total_2_hex3, m_total_2_hex4,
       m_total_2_hex5, m_total_2_hex6, m_total_3_hex0, m_total_3_hex1, m_total_3_hex2, m_total_3_hex3,
       m_total_3_hex4, m_total_3_hex5, m_total_3_hex6, m_total_4_hex0, m_total_4_hex1, m_total_4_hex2,
       m_total_4_hex3, m_total_4_hex4, m_total_4_hex5, m_total_4_hex6;
  wire [7:0] i0_1_s, i1_1_s, i2_1_s, i3_1_s, i4_1_s, i5_1_s;

  i0 i0_1 (.A(A), .S(i0_1_s));
  i1 i1_1 (.B(B), .A(A), .S(i1_1_s));
  i2 i2_1 (.A(A), .B(B), .S(i2_1_s));
  i3 i3_1 (.A(A), .B(B), .S(i3_1_s));
  i4 i4_1 (.A(A), .B(B), .S(i4_1_s));
  i5 i5_1 (.A(A), .B(B), .S(i5_1_s));
  m_total m_total_1 (
    .c3(B[3]), .c2(B[2]), .c1(B[1]), .c0(B[0]), .HEX0(m_total_1_hex0), .HEX1(m_total_1_hex1),
    .HEX2(m_total_1_hex2), .HEX3(m_total_1_hex3), .HEX4(m_total_1_hex4), .HEX5(m_total_1_hex5),
    .HEX6(m_total_1_hex6));
  m_total m_total_2 (
    .c3(A[3]), .c2(A[2]), .c1(A[1]), .c0(A[0]), .HEX0(m_total_2_hex0), .HEX1(m_total_2_hex1),
    .HEX2(m_total_2_hex2), .HEX3(m_total_2_hex3), .HEX4(m_total_2_hex4), .HEX5(m_total_2_hex5),
    .HEX6(m_total_2_hex6));
  _7_Segment_Display #(.active("false")) u_7_segment_display_1 (
    .g(m_total_1_hex6), .f(m_total_1_hex5), .a(m_total_1_hex0), .b(m_total_1_hex1), .e(m_total_1_hex4),
    .d(m_total_1_hex3), .c(m_total_1_hex2));  // open: dp
  _7_Segment_Display #(.active("false")) u_7_segment_display_2 (
    .g(m_total_2_hex6), .f(m_total_2_hex5), .a(m_total_2_hex0), .b(m_total_2_hex1), .e(m_total_2_hex4),
    .d(m_total_2_hex3), .c(m_total_2_hex2));  // open: dp
  mux6to1 mux6to1_1 (
    .a0(i0_1_s), .a1(i1_1_s), .a2(i2_1_s), .a3(i3_1_s), .a4(i4_1_s), .a5(i5_1_s), .S(C), .L(S[3:0]),
    .H(S[7:4]));  // open: a6, a7
  LED led_1 (.in(S[7]));
  m_total m_total_3 (
    .c3(S[3]), .c2(S[2]), .c1(S[1]), .c0(S[0]), .HEX0(m_total_3_hex0), .HEX1(m_total_3_hex1),
    .HEX2(m_total_3_hex2), .HEX3(m_total_3_hex3), .HEX4(m_total_3_hex4), .HEX5(m_total_3_hex5),
    .HEX6(m_total_3_hex6));
  m_total m_total_4 (
    .c3(S[7]), .c2(S[6]), .c1(S[5]), .c0(S[4]), .HEX0(m_total_4_hex0), .HEX1(m_total_4_hex1),
    .HEX2(m_total_4_hex2), .HEX3(m_total_4_hex3), .HEX4(m_total_4_hex4), .HEX5(m_total_4_hex5),
    .HEX6(m_total_4_hex6));
  LED led_2 (.in(S[0]));
  LED led_3 (.in(S[5]));
  LED led_4 (.in(S[6]));
  LED led_5 (.in(S[1]));
  LED led_6 (.in(S[2]));
  LED led_7 (.in(S[3]));
  LED led_8 (.in(S[4]));
  _7_Segment_Display #(.active("false")) u_7_segment_display_3 (
    .g(m_total_3_hex6), .f(m_total_3_hex5), .a(m_total_3_hex0), .b(m_total_3_hex1), .e(m_total_3_hex4),
    .d(m_total_3_hex3), .c(m_total_3_hex2));  // open: dp
  _7_Segment_Display #(.active("false")) u_7_segment_display_4 (
    .g(m_total_4_hex6), .f(m_total_4_hex5), .a(m_total_4_hex0), .b(m_total_4_hex1), .e(m_total_4_hex4),
    .d(m_total_4_hex3), .c(m_total_4_hex2));  // open: dp
endmodule

module segment (
  input  SW_3,
  input  SW_2,
  input  SW_1,
  input  SW_0
);

  wire m_total_1_hex0, m_total_1_hex1, m_total_1_hex2, m_total_1_hex3, m_total_1_hex4, m_total_1_hex5,
       m_total_1_hex6;

  m_total m_total_1 (
    .c3(SW_3), .c2(SW_2), .c1(SW_1), .c0(SW_0), .HEX0(m_total_1_hex0), .HEX1(m_total_1_hex1),
    .HEX2(m_total_1_hex2), .HEX3(m_total_1_hex3), .HEX4(m_total_1_hex4), .HEX5(m_total_1_hex5),
    .HEX6(m_total_1_hex6));
  _7_Segment_Display #(.active("false")) L_7_Segment_Display_1 (
    .g(m_total_1_hex6), .f(m_total_1_hex5), .a(m_total_1_hex0), .b(m_total_1_hex1), .e(m_total_1_hex4),
    .d(m_total_1_hex3), .c(m_total_1_hex2));  // open: dp
endmodule

module m_total (
  input  c3,
  input  c2,
  input  c1,
  input  c0,
  output HEX0,
  output HEX1,
  output HEX2,
  output HEX3,
  output HEX4,
  output HEX5,
  output HEX6
);

  M0 M0_1 (.c0(c0), .c1(c1), .c2(c2), .c3(c3), .HEX0(HEX0));
  M1 M1_1 (.c3(c3), .c2(c2), .c1(c1), .c0(c0), .HEX1(HEX1));
  M2 M2_1 (.c3(c3), .c2(c2), .c1(c1), .c0(c0), .HEX2(HEX2));
  M3 M3_1 (.c3(c3), .c2(c2), .c1(c1), .c0(c0), .HEX3(HEX3));
  M4 M4_1 (.c3(c3), .c2(c2), .c1(c1), .c0(c0), .HEX4(HEX4));
  M5 M5_1 (.c3(c3), .c2(c2), .c1(c1), .c0(c0), .HEX5(HEX5));
  M6 M6_1 (.c3(c3), .c2(c2), .c1(c1), .c0(c0), .HEX6(HEX6));
endmodule

module M0 (
  input  c0,
  input  c1,
  input  c2,
  input  c3,
  output HEX0
);

  wire and_1_out, and_2_out, and_3_out, and_4_out, not_1_out, not_2_out, not_3_out, not_4_out, not_5_out;

  not not_1 (not_1_out, c1);
  not not_2 (not_2_out, c2);
  not not_3 (not_3_out, c3);
  not not_4 (not_4_out, c0);
  and and_1 (and_1_out, not_4_out, not_1_out, c2, not_3_out);
  not not_5 (not_5_out, c2);
  and and_2 (and_2_out, not_3_out, not_5_out, not_1_out, c0);
  and and_3 (and_3_out, c0, not_1_out, c2, c3);
  and and_4 (and_4_out, c0, c1, not_2_out, c3);
  or or_1 (HEX0, and_1_out, and_2_out, and_3_out, and_4_out);
endmodule

module M1 (
  input  c3,
  input  c2,
  input  c1,
  input  c0,
  output HEX1
);

  wire and_1_out, and_2_out, and_3_out, and_4_out, not_1_out, not_2_out, not_3_out;

  not not_1 (not_1_out, c3);
  not not_2 (not_2_out, c1);
  not not_3 (not_3_out, c0);
  and and_1 (and_1_out, not_1_out, c2, not_2_out, c0);
  and and_2 (and_2_out, c3, c2, not_3_out);
  and and_3 (and_3_out, c3, c1, c0);
  and and_4 (and_4_out, c2, c1, not_3_out);
  or or_1 (HEX1, and_1_out, and_4_out, and_2_out, and_3_out);
endmodule

module M2 (
  input  c3,
  input  c2,
  input  c1,
  input  c0,
  output HEX2
);

  wire and_1_out, and_2_out, and_3_out, not_1_out, not_2_out, not_3_out;

  not not_1 (not_1_out, c3);
  not not_2 (not_2_out, c2);
  not not_3 (not_3_out, c0);
  and and_1 (and_1_out, not_1_out, not_2_out, c1, not_3_out);
  and and_2 (and_2_out, c3, c2, not_3_out);
  and and_3 (and_3_out, c3, c2, c1);
  or or_1 (HEX2, and_1_out, and_3_out, and_2_out);
endmodule

module M3 (
  input  c3,
  input  c2,
  input  c1,
  input  c0,
  output HEX3
);

  wire and_1_out, and_2_out, and_3_out, and_4_out, not_1_out, not_2_out, not_3_out, not_4_out;

  not not_1 (not_1_out, c2);
  not not_2 (not_2_out, c3);
  not not_3 (not_3_out, c1);
  not not_4 (not_4_out, c0);
  and and_1 (and_1_out, not_2_out, c2, not_3_out, not_4_out);
  and and_2 (and_2_out, not_1_out, not_3_out, c0);
  and and_3 (and_3_out, c2, c1, c0);
  and and_4 (and_4_out, c3, not_1_out, c1, not_4_out);
  or or_1 (HEX3, and_1_out, and_4_out, and_2_out, and_3_out);
endmodule

module M4 (
  input  c3,
  input  c2,
  input  c1,
  input  c0,
  output HEX4
);

  wire and_1_out, and_2_out, and_3_out, not_1_out, not_2_out, not_3_out;

  not not_1 (not_1_out, c2);
  not not_2 (not_2_out, c3);
  not not_3 (not_3_out, c1);
  and and_1 (and_1_out, not_2_out, c2, not_3_out);
  and and_2 (and_2_out, not_2_out, c0);
  and and_3 (and_3_out, not_1_out, not_3_out, c0);
  or or_1 (HEX4, and_1_out, and_2_out, and_3_out);
endmodule

module M5 (
  input  c3,
  input  c2,
  input  c1,
  input  c0,
  output HEX5
);

  wire and_1_out, and_2_out, and_3_out, and_4_out, not_1_out, not_2_out, not_3_out;

  not not_1 (not_1_out, c3);
  not not_2 (not_2_out, c2);
  not not_3 (not_3_out, c1);
  and and_1 (and_1_out, c3, c2, not_3_out, c0);
  and and_2 (and_2_out, not_1_out, not_2_out, c0);
  and and_3 (and_3_out, not_1_out, c1, c0);
  and and_4 (and_4_out, not_1_out, not_2_out, c1);
  or or_1 (HEX5, and_1_out, and_2_out, and_3_out, and_4_out);
endmodule

module M6 (
  input  c3,
  input  c2,
  input  c1,
  input  c0,
  output HEX6
);

  wire and_1_out, and_2_out, and_3_out, not_1_out, not_2_out, not_3_out, not_4_out;

  not not_1 (not_1_out, c3);
  not not_2 (not_2_out, c2);
  not not_3 (not_3_out, c1);
  not not_4 (not_4_out, c0);
  and and_1 (and_1_out, not_1_out, not_2_out, not_3_out);
  and and_2 (and_2_out, c3, c2, not_3_out, not_4_out);
  and and_3 (and_3_out, c0, c1, c2, not_1_out);
  or or_1 (HEX6, and_1_out, and_2_out, and_3_out);
endmodule

module FA (
  input  c_in,
  input  B,
  input  A,
  output s,
  output c_out
);

  wire xor_1_out;

  xor xor_1 (xor_1_out, B, A);
  Multiplexer #(.enable("false")) multiplexer_1 (.in0(A), .in1(c_in), .out(c_out), .sel(xor_1_out));
  xor xor_2 (s, c_in, xor_1_out);
endmodule

module ripple_adder (
  input  c_in,
  input  [3:0] a,
  input  [3:0] b,
  output LEDR_1,
  output LEDR_2,
  output LEDR_0,
  output LEDR_3,
  output LEDR_4
);

  wire fa_2_c_out, fa_3_c_out, fa_4_c_out;

  FA fa_1 (.c_in(fa_2_c_out), .B(b[3]), .A(a[3]), .s(LEDR_3), .c_out(LEDR_4));
  FA fa_2 (.c_in(fa_3_c_out), .B(b[2]), .A(a[2]), .s(LEDR_2), .c_out(fa_2_c_out));
  FA fa_3 (.c_in(fa_4_c_out), .B(b[1]), .A(a[1]), .s(LEDR_1), .c_out(fa_3_c_out));
  FA fa_4 (.c_in(c_in), .B(b[0]), .A(a[0]), .s(LEDR_0), .c_out(fa_4_c_out));
endmodule

module i0 (
  input  [3:0] A,
  output [7:0] S
);

  wire [4:0] ripple_adder_1_ledr_0;

  ripple_adder ripple_adder_1 (
    .c_in(1'b1), .a(A), .b(4'b0000), .LEDR_1(ripple_adder_1_ledr_0[1]), .LEDR_2(ripple_adder_1_ledr_0[2]),
    .LEDR_0(ripple_adder_1_ledr_0[0]), .LEDR_3(ripple_adder_1_ledr_0[3]), .LEDR_4(ripple_adder_1_ledr_0[4]));
  assign S = {{3{1'b0}}, ripple_adder_1_ledr_0};  // Bit_Extender bit_extender_1
endmodule

module i1 (
  input  [3:0] B,
  input  [3:0] A,
  output [7:0] S
);

  wire [4:0] ripple_adder_1_ledr_0;

  ripple_adder ripple_adder_1 (
    .c_in(1'b0), .a(B), .b(A), .LEDR_1(ripple_adder_1_ledr_0[1]), .LEDR_2(ripple_adder_1_ledr_0[2]),
    .LEDR_0(ripple_adder_1_ledr_0[0]), .LEDR_3(ripple_adder_1_ledr_0[3]), .LEDR_4(ripple_adder_1_ledr_0[4]));
  assign S = {{3{1'b0}}, ripple_adder_1_ledr_0};  // Bit_Extender bit_extender_1
endmodule

module i2 (
  input  [3:0] A,
  input  [3:0] B,
  output [7:0] S
);

  wire adder_1_cout;
  wire [3:0] adder_1_out;
  wire [4:0] bit_extender_1_out;

  Adder #(.width(4)) adder_1 (.a(A), .b(B), .out(adder_1_out), .cout(adder_1_cout));  // open: cin
  assign bit_extender_1_out = {{1{adder_1_cout}}, adder_1_out};  // Bit_Extender bit_extender_1
  assign S = {{3{1'b0}}, bit_extender_1_out};  // Bit_Extender bit_extender_2
endmodule

module i3 (
  input  [3:0] A,
  input  [3:0] B,
  output [7:0] S
);

  assign S[3:0] = A ^ B;  // XOR_Gate xor_1, 4 bits wide
  assign S[7:4] = A | B;  // OR_Gate or_1, 4 bits wide
endmodule

module i4 (
  input  [3:0] A,
  input  [3:0] B,
  output [7:0] S
);

  wire or_1_out;

  or or_1 (or_1_out, A[0], A[1], A[2], A[3], B[0], B[1], B[2], B[3]);
  assign S = {{7{1'b0}}, or_1_out};  // Bit_Extender bit_extender_1
endmodule

module i5 (
  input  [3:0] A,
  input  [3:0] B,
  output [7:0] S
);


  assign S = {A, B};
endmodule

module mux6to1 (
  input  [7:0] a0,
  input  [7:0] a1,
  input  [7:0] a2,
  input  [7:0] a3,
  input  [7:0] a4,
  input  [7:0] a5,
  input  [7:0] a6,
  input  [7:0] a7,
  input  [2:0] S,
  output [3:0] L,
  output [3:0] H
);

  Multiplexer #(.enable("false"), .select(3), .width(8)) multiplexer_1 (
    .in0(a0), .in1(a1), .in2(a2), .in3(a3), .in4(a4), .in5(a5), .in6(a6), .in7(a7), .out({H, L}), .sel(S));
endmodule

module left_shift (
  input  [3:0] B,
  input  [3:0] A,
  output [7:0] S
);

  wire [8:0] bit_extender_1_out;
  wire [8:8] shifter_1_out;

  assign bit_extender_1_out = {{5{1'b0}}, B};  // Bit_Extender bit_extender_1
  Shifter #(.width(9)) shifter_1 (.in(bit_extender_1_out), .\dist (A), .out({shifter_1_out[8], S}));
endmodule

module right_shift (
  input  [3:0] B,
  input  [3:0] A,
  output [7:0] S
);

  wire [8:0] bit_extender_1_out;
  wire [8:8] shifter_1_out;

  assign bit_extender_1_out = {{5{1'b0}}, B};  // Bit_Extender bit_extender_1
  Shifter #(.shift("lr"), .width(9)) shifter_1 (.in(bit_extender_1_out), .\dist (A), .out({shifter_1_out[8], S}));
endmodule

module i7 (
  input  [3:0] A,
  input  [3:0] B,
  output [7:0] S
);

  Multiplier #(.width(4)) multiplier_1 (.a(A), .b(B), .out(S[3:0]), .cout(S[7:4]));  // open: cin
endmodule

module ALU (
  input  [3:0] A,
  input  [3:0] B,
  input  [2:0] C,
  output [7:0] S
);

  wire m_total_1_hex0, m_total_1_hex1, m_total_1_hex2, m_total_1_hex3, m_total_1_hex4, m_total_1_hex5,
       m_total_1_hex6, m_total_2_hex0, m_total_2_hex1, m_total_2_hex2, m_total_2_hex3, m_total_2_hex4,
       m_total_2_hex5, m_total_2_hex6, m_total_3_hex0, m_total_3_hex1, m_total_3_hex2, m_total_3_hex3,
       m_total_3_hex4, m_total_3_hex5, m_total_3_hex6, m_total_4_hex0, m_total_4_hex1, m_total_4_hex2,
       m_total_4_hex3, m_total_4_hex4, m_total_4_hex5, m_total_4_hex6;
  wire [7:0] i0_1_s, i1_1_s, i2_1_s, i3_1_s, i4_1_s, i7_1_s, left_shift_1_s, right_shift_1_s;

  i0 i0_1 (.A(A), .S(i0_1_s));
  i1 i1_1 (.B(B), .A(A), .S(i1_1_s));
  i2 i2_1 (.A(A), .B(B), .S(i2_1_s));
  i3 i3_1 (.A(A), .B(B), .S(i3_1_s));
  i4 i4_1 (.A(A), .B(B), .S(i4_1_s));
  left_shift left_shift_1 (.B(A), .A(B), .S(left_shift_1_s));
  right_shift right_shift_1 (.B(A), .A(B), .S(right_shift_1_s));
  i7 i7_1 (.A(A), .B(B), .S(i7_1_s));
  m_total m_total_1 (
    .c3(B[3]), .c2(B[2]), .c1(B[1]), .c0(B[0]), .HEX0(m_total_1_hex0), .HEX1(m_total_1_hex1),
    .HEX2(m_total_1_hex2), .HEX3(m_total_1_hex3), .HEX4(m_total_1_hex4), .HEX5(m_total_1_hex5),
    .HEX6(m_total_1_hex6));
  m_total m_total_2 (
    .c3(A[3]), .c2(A[2]), .c1(A[1]), .c0(A[0]), .HEX0(m_total_2_hex0), .HEX1(m_total_2_hex1),
    .HEX2(m_total_2_hex2), .HEX3(m_total_2_hex3), .HEX4(m_total_2_hex4), .HEX5(m_total_2_hex5),
    .HEX6(m_total_2_hex6));
  mux6to1 mux6to1_1 (
    .a0(i0_1_s), .a1(i1_1_s), .a2(i2_1_s), .a3(i3_1_s), .a4(i4_1_s), .a5(left_shift_1_s),
    .a6(right_shift_1_s), .a7(i7_1_s), .S(C), .L(S[3:0]), .H(S[7:4]));
  _7_Segment_Display #(.active("false")) u_7_segment_display_1 (
    .g(m_total_1_hex6), .f(m_total_1_hex5), .a(m_total_1_hex0), .b(m_total_1_hex1), .e(m_total_1_hex4),
    .d(m_total_1_hex3), .c(m_total_1_hex2));  // open: dp
  _7_Segment_Display #(.active("false")) u_7_segment_display_2 (
    .g(m_total_2_hex6), .f(m_total_2_hex5), .a(m_total_2_hex0), .b(m_total_2_hex1), .e(m_total_2_hex4),
    .d(m_total_2_hex3), .c(m_total_2_hex2));  // open: dp
  LED led_1 (.in(S[7]));
  m_total m_total_3 (
    .c3(S[3]), .c2(S[2]), .c1(S[1]), .c0(S[0]), .HEX0(m_total_3_hex0), .HEX1(m_total_3_hex1),
    .HEX2(m_total_3_hex2), .HEX3(m_total_3_hex3), .HEX4(m_total_3_hex4), .HEX5(m_total_3_hex5),
    .HEX6(m_total_3_hex6));
  m_total m_total_4 (
    .c3(S[7]), .c2(S[6]), .c1(S[5]), .c0(S[4]), .HEX0(m_total_4_hex0), .HEX1(m_total_4_hex1),
    .HEX2(m_total_4_hex2), .HEX3(m_total_4_hex3), .HEX4(m_total_4_hex4), .HEX5(m_total_4_hex5),
    .HEX6(m_total_4_hex6));
  LED led_2 (.in(S[0]));
  LED led_3 (.in(S[5]));
  LED led_4 (.in(S[6]));
  LED led_5 (.in(S[1]));
  LED led_6 (.in(S[2]));
  LED led_7 (.in(S[3]));
  LED led_8 (.in(S[4]));
  _7_Segment_Display #(.active("false")) u_7_segment_display_3 (
    .g(m_total_3_hex6), .f(m_total_3_hex5), .a(m_total_3_hex0), .b(m_total_3_hex1), .e(m_total_3_hex4),
    .d(m_total_3_hex3), .c(m_total_3_hex2));  // open: dp
  _7_Segment_Display #(.active("false")) u_7_segment_display_4 (
    .g(m_total_4_hex6), .f(m_total_4_hex5), .a(m_total_4_hex0), .b(m_total_4_hex1), .e(m_total_4_hex4),
    .d(m_total_4_hex3), .c(m_total_4_hex2));  // open: dp
endmodule
