// Logisim project lab4_part3.circ as structural Verilog: 3 circuits, main circuit main
module main (
  input  [7:0] loadVal,
  input  ShiftRight,
  input  load_n,
  input  clk,
  input  reset,
  input  ASR,
  output [7:0] s
);

  wire mux2_1_m;

  mux2 mux2_1 (.x(1'b0), .y(s[7]), .s(ASR), .m(mux2_1_m));
  Shifterbit sb0 (.i(s[1]), .l_v(loadVal[0]), .shift(ShiftRight), .l_n(load_n), .clk(clk), .r(reset), .s(s[0]));
  Shifterbit sb1 (.i(s[2]), .l_v(loadVal[1]), .shift(ShiftRight), .l_n(load_n), .clk(clk), .r(reset), .s(s[1]));
  Shifterbit sb2 (.i(s[3]), .l_v(loadVal[2]), .shift(ShiftRight), .l_n(load_n), .clk(clk), .r(reset), .s(s[2]));
  Shifterbit sb3 (.i(s[4]), .l_v(loadVal[3]), .shift(ShiftRight), .l_n(load_n), .clk(clk), .r(reset), .s(s[3]));
  Shifterbit sb4 (.i(s[5]), .l_v(loadVal[4]), .shift(ShiftRight), .l_n(load_n), .clk(clk), .r(reset), .s(s[4]));
  Shifterbit sb5 (.i(s[6]), .l_v(loadVal[5]), .shift(ShiftRight), .l_n(load_n), .clk(clk), .r(reset), .s(s[5]));
  Shifterbit sb6 (.i(s[7]), .l_v(loadVal[6]), .shift(ShiftRight), .l_n(load_n), .clk(clk), .r(reset), .s(s[6]));
  Shifterbit sb7 (.i(mux2_1_m), .l_v(loadVal[7]), .shift(ShiftRight), .l_n(load_n), .clk(clk), .r(reset), .s(s[7]));
endmodule

module mux2 (
  input  x,
  input  y,
  input  s,
  output m
);

  Multiplexer #(.enable("false")) multiplexer_1 (.in0(x), .in1(y), .out(m), .sel(s));
endmodule

module Shifterbit (
  input  i,
  input  l_v,
  input  shift,
  input  l_n,
  input  clk,
  input  r,
  output s
);

  wire mux2_1_m, mux2_2_m;

  mux2 mux2_1 (.x(s), .y(i), .s(shift), .m(mux2_1_m));
  mux2 mux2_2 (.x(l_v), .y(mux2_1_m), .s(l_n), .m(mux2_2_m));
  D_Flip_Flop d_ff_1 (.D(mux2_2_m), .clk(clk), .Q(s), .reset(r));  // open: Qn, preset
endmodule
