// Logisim project lab5_part1.circ as structural Verilog: 9 circuits, main circuit M0
module main (
  input  Enable,
  input  Clk,
  input  Clear_b
);

  wire and_1_out, and_2_out, and_3_out, and_4_out, and_5_out, and_6_out, and_7_out, m_total_1_hex0,
       m_total_1_hex1, m_total_1_hex2, m_total_1_hex3, m_total_1_hex4, m_total_1_hex5, m_total_1_hex6,
       m_total_2_hex0, m_total_2_hex1, m_total_2_hex2, m_total_2_hex3, m_total_2_hex4, m_total_2_hex5,
       m_total_2_hex6, Q_0_q, Q_1_q, Q_2_q, Q_3_q, Q_4_q, Q_5_q, Q_6_q, Q_7_q;

  T_Flip_Flop Q_0 (.T(Enable), .clk(Clk), .Q(Q_0_q), .reset(Clear_b));  // open: Qn, preset
  and and_1 (and_1_out, Enable, Q_0_q);
  T_Flip_Flop Q_1 (.T(and_1_out), .clk(Clk), .Q(Q_1_q), .reset(Clear_b));  // open: Qn, preset
  and and_2 (and_2_out, and_1_out, Q_1_q);
  T_Flip_Flop Q_2 (.T(and_2_out), .clk(Clk), .Q(Q_2_q), .reset(Clear_b));  // open: Qn, preset
  and and_3 (and_3_out, and_2_out, Q_2_q);
  T_Flip_Flop Q_3 (.T(and_3_out), .clk(Clk), .Q(Q_3_q), .reset(Clear_b));  // open: Qn, preset
  m_total m_total_1 (
    .c3(Q_7_q), .c2(Q_6_q), .c1(Q_5_q), .c0(Q_4_q), .HEX0(m_total_1_hex0), .HEX1(m_total_1_hex1),
    .HEX2(m_total_1_hex2), .HEX3(m_total_1_hex3), .HEX4(m_total_1_hex4), .HEX5(m_total_1_hex5),
    .HEX6(m_total_1_hex6));
  and and_4 (and_4_out, and_3_out, Q_3_q);
  T_Flip_Flop Q_4 (.T(and_4_out), .clk(Clk), .Q(Q_4_q), .reset(Clear_b));  // open: Qn, preset
  _7_Segment_Display #(.active("false")) u_7_segment_display_1 (
    .g(m_total_1_hex6), .f(m_total_1_hex5), .a(m_total_1_hex0), .b(m_total_1_hex1), .e(m_total_1_hex4),
    .d(m_total_1_hex3), .c(m_total_1_hex2));  // open: dp
  and and_5 (and_5_out, and_4_out, Q_4_q);
  T_Flip_Flop Q_5 (.T(and_5_out), .clk(Clk), .Q(Q_5_q), .reset(Clear_b));  // open: Qn, preset
  m_total m_total_2 (
    .c3(Q_3_q), .c2(Q_2_q), .c1(Q_1_q), .c0(Q_0_q), .HEX0(m_total_2_hex0), .HEX1(m_total_2_hex1),
    .HEX2(m_total_2_hex2), .HEX3(m_total_2_hex3), .HEX4(m_total_2_hex4), .HEX5(m_total_2_hex5),
    .HEX6(m_total_2_hex6));
  and and_6 (and_6_out, and_5_out, Q_5_q);
  T_Flip_Flop Q_6 (.T(and_6_out), .clk(Clk), .Q(Q_6_q), .reset(Clear_b));  // open: Qn, preset
  _7_Segment_Display #(.active("false")) u_7_segment_display_2 (
    .g(m_total_2_hex6), .f(m_total_2_hex5), .a(m_total_2_hex0), .b(m_total_2_hex1), .e(m_total_2_hex4),
    .d(m_total_2_hex3), .c(m_total_2_hex2));  // open: dp
  and and_7 (and_7_out, and_6_out, Q_6_q);
  T_Flip_Flop Q_7 (.T(and_7_out), .clk(Clk), .Q(Q_7_q), .reset(Clear_b));  // open: Qn, preset
endmodule

module m_total (
  input  c3,
  input  c2,
  input  c1,
  input  c0,
  output HEX0,
  output HEX1,
  output HEX2,
  output HEX3,
  output HEX4,
  output HEX5,
  output HEX6
);

  M0 M0_1 (.c0(c0), .c1(c1), .c2(c2), .c3(c3), .HEX0(HEX0));
  M1 M1_1 (.c3(c3), .c2(c2), .c1(c1), .c0(c0), .HEX1(HEX1));
  M2 M2_1 (.c3(c3), .c2(c2), .c1(c1), .c0(c0), .HEX2(HEX2));
  M3 M3_1 (.c3(c3), .c2(c2), .c1(c1), .c0(c0), .HEX3(HEX3));
  M4 M4_1 (.c3(c3), .c2(c2), .c1(c1), .c0(c0), .HEX4(HEX4));
  M5 M5_1 (.c3(c3), .c2(c2), .c1(c1), .c0(c0), .HEX5(HEX5));
  M6 M6_1 (.c3(c3), .c2(c2), .c1(c1), .c0(c0), .HEX6(HEX6));
endmodule

module M0 (
  input  c0,
  input  c1,
  input  c2,
  input  c3,
  output HEX0
);

  wire and_1_out, and_2_out, and_3_out, and_4_out, not_1_out, not_2_out, not_3_out, not_4_out, not_5_out;

  not not_1 (not_1_out, c1);
  not not_2 (not_2_out, c2);
  not not_3 (not_3_out, c3);
  not not_4 (not_4_out, c0);
  and and_1 (and_1_out, not_4_out, not_1_out, c2, not_3_out);
  not not_5 (not_5_out, c2);
  and and_2 (and_2_out, not_3_out, not_5_out, not_1_out, c0);
  and and_3 (and_3_out, c0, not_1_out, c2, c3);
  and and_4 (and_4_out, c0, c1, not_2_out, c3);
  or or_1 (HEX0, and_1_out, and_2_out, and_3_out, and_4_out);
endmodule

module M1 (
  input  c3,
  input  c2,
  input  c1,
  input  c0,
  output HEX1
);

  wire and_1_out, and_2_out, and_3_out, and_4_out, not_1_out, not_2_out, not_3_out;

  not not_1 (not_1_out, c3);
  not not_2 (not_2_out, c1);
  not not_3 (not_3_out, c0);
  and and_1 (and_1_out, not_1_out, c2, not_2_out, c0);
  and and_2 (and_2_out, c3, c2, not_3_out);
  and and_3 (and_3_out, c3, c1, c0);
  and and_4 (and_4_out, c2, c1, not_3_out);
  or or_1 (HEX1, and_1_out, and_4_out, and_2_out, and_3_out);
endmodule

module M2 (
  input  c3,
  input  c2,
  input  c1,
  input  c0,
  output HEX2
);

  wire and_1_out, and_2_out, and_3_out, not_1_out, not_2_out, not_3_out;

  not not_1 (not_1_out, c3);
  not not_2 (not_2_out, c2);
  not not_3 (not_3_out, c0);
  and and_1 (and_1_out, not_1_out, not_2_out, c1, not_3_out);
  and and_2 (and_2_out, c3, c2, not_3_out);
  and and_3 (and_3_out, c3, c2, c1);
  or or_1 (HEX2, and_1_out, and_3_out, and_2_out);
endmodule

module M3 (
  input  c3,
  input  c2,
  input  c1,
  input  c0,
  output HEX3
);

  wire and_1_out, and_2_out, and_3_out, and_4_out, not_1_out, not_2_out, not_3_out, not_4_out;

  not not_1 (not_1_out, c2);
  not not_2 (not_2_out, c3);
  not not_3 (not_3_out, c1);
  not not_4 (not_4_out, c0);
  and and_1 (and_1_out, not_2_out, c2, not_3_out, not_4_out);
  and and_2 (and_2_out, not_1_out, not_3_out, c0);
  and and_3 (and_3_out, c2, c1, c0);
  and and_4 (and_4_out, c3, not_1_out, c1, not_4_out);
  or or_1 (HEX3, and_1_out, and_4_out, and_2_out, and_3_out);
endmodule

module M4 (
  input  c3,
  input  c2,
  input  c1,
  input  c0,
  output HEX4
);

  wire and_1_out, and_2_out, and_3_out, not_1_out, not_2_out, not_3_out;

  not not_1 (not_1_out, c2);
  not not_2 (not_2_out, c3);
  not not_3 (not_3_out, c1);
  and and_1 (and_1_out, not_2_out, c2, not_3_out);
  and and_2 (and_2_out, not_2_out, c0);
  and and_3 (and_3_out, not_1_out, not_3_out, c0);
  or or_1 (HEX4, and_1_out, and_2_out, and_3_out);
endmodule

module M5 (
  input  c3,
  input  c2,
  input  c1,
  input  c0,
  output HEX5
);

  wire and_1_out, and_2_out, and_3_out, and_4_out, not_1_out, not_2_out, not_3_out;

  not not_1 (not_1_out, c3);
  not not_2 (not_2_out, c2);
  not not_3 (not_3_out, c1);
  and and_1 (and_1_out, c3, c2, not_3_out, c0);
  and and_2 (and_2_out, not_1_out, not_2_out, c0);
  and and_3 (and_3_out, not_1_out, c1, c0);
  and and_4 (and_4_out, not_1_out, not_2_out, c1);
  or or_1 (HEX5, and_1_out, and_2_out, and_3_out, and_4_out);
endmodule

module M6 (
  input  c3,
  input  c2,
  input  c1,
  input  c0,
  output HEX6
);

  wire and_1_out, and_2_out, and_3_out, not_1_out, not_2_out, not_3_out, not_4_out;

  not not_1 (not_1_out, c3);
  not not_2 (not_2_out, c2);
  not not_3 (not_3_out, c1);
  not not_4 (not_4_out, c0);
  and and_1 (and_1_out, not_1_out, not_2_out, not_3_out);
  and and_2 (and_2_out, c3, c2, not_3_out, not_4_out);
  and and_3 (and_3_out, c0, c1, c2, not_1_out);
  or or_1 (HEX6, and_1_out, and_2_out, and_3_out);
endmodule
