// Logisim project lab5_part2.circ as structural Verilog: 14 circuits, main circuit main
module main (
  input  reset,
  input  enable,
  input  [1:0] SW
);

  wire clock_1_out, m_total_1_hex0, m_total_1_hex1, m_total_1_hex2, m_total_1_hex3, m_total_1_hex4,
       m_total_1_hex5, m_total_1_hex6, ratedivider_1_s;
  wire [3:0] counter_1_q;

  Clock clock_1 (.out(clock_1_out));
  ratedivider ratedivider_1 (.clk(clock_1_out), .reset(reset), .enable(enable), .sw(SW), .S(ratedivider_1_s));
  Counter #(.max('hf), .width(4)) counter_1 (
    .clr(reset), .load(1'b0), .up(1'b1), .count(ratedivider_1_s), .clk(clock_1_out), .D(4'b0000),
    .Q(counter_1_q));  // open: carry
  m_total m_total_1 (
    .c3(counter_1_q[3]), .c2(counter_1_q[2]), .c1(counter_1_q[1]), .c0(counter_1_q[0]),
    .HEX0(m_total_1_hex0), .HEX1(m_total_1_hex1), .HEX2(m_total_1_hex2), .HEX3(m_total_1_hex3),
    .HEX4(m_total_1_hex4), .HEX5(m_total_1_hex5), .HEX6(m_total_1_hex6));
  _7_Segment_Display #(.active("false")) u_7_segment_display_1 (
    .g(m_total_1_hex6), .f(m_total_1_hex5), .a(m_total_1_hex0), .b(m_total_1_hex1), .e(m_total_1_hex4),
    .d(m_total_1_hex3), .c(m_total_1_hex2));  // open: dp
endmodule

module ratedivider (
  input  clk,
  input  reset,
  input  enable,
  input  [1:0] sw,
  output S
);

  wire and_1_out, and_2_out, and_3_out, counter_1_q, not_1_out, or_1_out;
  wire [3:0] counter_2_q;
  wire [4:0] counter_3_q;
  wire [5:0] counter_4_q;

  not not_1 (not_1_out, enable);
  or or_1 (or_1_out, S, not_1_out);
  Counter #(.max('h1), .width(1)) counter_1 (
    .clr(reset), .load(or_1_out), .up(1'b1), .clk(clk), .D(1'b0), .Q(counter_1_q));  // open: count, carry
  Counter #(.max('hf), .width(4)) counter_2 (
    .clr(reset), .load(or_1_out), .up(1'b1), .clk(clk), .D(4'b0000), .Q(counter_2_q));  // open: count, carry
  Counter #(.max('h1f), .width(5)) counter_3 (
    .clr(reset), .load(or_1_out), .up(1'b1), .clk(clk), .D({5{1'b0}}), .Q(counter_3_q));  // open: count, carry
  Counter #(.max('h3f), .width(6)) counter_4 (
    .clr(reset), .load(or_1_out), .up(1'b1), .clk(clk), .D({6{1'b0}}), .Q(counter_4_q));  // open: count, carry
  and and_1 (and_1_out, counter_2_q[0], counter_2_q[1], counter_2_q[2], counter_2_q[3]);
  and and_2 (and_2_out, counter_3_q[0], counter_3_q[1], counter_3_q[2], counter_3_q[3], counter_3_q[4]);
  and and_3 (and_3_out, counter_4_q[0], counter_4_q[1], counter_4_q[2], counter_4_q[3], counter_4_q[4], counter_4_q[5]);
  Multiplexer #(.enable("false"), .select(2)) multiplexer_1 (
    .in0(counter_1_q), .in1(and_1_out), .in2(and_2_out), .in3(and_3_out), .out(S), .sel(sw));
endmodule

module divideBy2 (
  input  i,
  output s
);

  wire d_ff_1_qn;

  D_Flip_Flop d_ff_1 (.D(d_ff_1_qn), .clk(i), .Q(s), .Qn(d_ff_1_qn));  // open: preset, reset
endmodule

module displaycounter (
  input  clear,
  input  clk,
  input  enable,
  output [3:0] s
);

  wire and_1_out, not_1_out, or_1_out;

  not not_1 (not_1_out, enable);
  or or_1 (or_1_out, and_1_out, not_1_out);
  Counter #(.max('hf), .width(4)) counter_1 (
    .clr(clear), .load(or_1_out), .up(1'b1), .clk(clk), .D(4'b0000), .Q(s));  // open: count, carry
  and and_1 (and_1_out, s[0], s[1], s[2], s[3]);
endmodule

module m_total (
  input  c3,
  input  c2,
  input  c1,
  input  c0,
  output HEX0,
  output HEX1,
  output HEX2,
  output HEX3,
  output HEX4,
  output HEX5,
  output HEX6
);

  M0 M0_1 (.c0(c0), .c1(c1), .c2(c2), .c3(c3), .HEX0(HEX0));
  M1 M1_1 (.c3(c3), .c2(c2), .c1(c1), .c0(c0), .HEX1(HEX1));
  M2 M2_1 (.c3(c3), .c2(c2), .c1(c1), .c0(c0), .HEX2(HEX2));
  M3 M3_1 (.c3(c3), .c2(c2), .c1(c1), .c0(c0), .HEX3(HEX3));
  M4 M4_1 (.c3(c3), .c2(c2), .c1(c1), .c0(c0), .HEX4(HEX4));
  M5 M5_1 (.c3(c3), .c2(c2), .c1(c1), .c0(c0), .HEX5(HEX5));
  M6 M6_1 (.c3(c3), .c2(c2), .c1(c1), .c0(c0), .HEX6(HEX6));
endmodule

module M0 (
  input  c0,
  input  c1,
  input  c2,
  input  c3,
  output HEX0
);

  wire and_1_out, and_2_out, and_3_out, and_4_out, not_1_out, not_2_out, not_3_out, not_4_out, not_5_out;

  not not_1 (not_1_out, c1);
  not not_2 (not_2_out, c2);
  not not_3 (not_3_out, c3);
  not not_4 (not_4_out, c0);
  and and_1 (and_1_out, not_4_out, not_1_out, c2, not_3_out);
  not not_5 (not_5_out, c2);
  and and_2 (and_2_out, not_3_out, not_5_out, not_1_out, c0);
  and and_3 (and_3_out, c0, not_1_out, c2, c3);
  and and_4 (and_4_out, c0, c1, not_2_out, c3);
  or or_1 (HEX0, and_1_out, and_2_out, and_3_out, and_4_out);
endmodule

module M1 (
  input  c3,
  input  c2,
  input  c1,
  input  c0,
  output HEX1
);

  wire and_1_out, and_2_out, and_3_out, and_4_out, not_1_out, not_2_out, not_3_out;

  not not_1 (not_1_out, c3);
  not not_2 (not_2_out, c1);
  not not_3 (not_3_out, c0);
  and and_1 (and_1_out, not_1_out, c2, not_2_out, c0);
  and and_2 (and_2_out, c3, c2, not_3_out);
  and and_3 (and_3_out, c3, c1, c0);
  and and_4 (and_4_out, c2, c1, not_3_out);
  or or_1 (HEX1, and_1_out, and_4_out, and_2_out, and_3_out);
endmodule

module M2 (
  input  c3,
  input  c2,
  input  c1,
  input  c0,
  output HEX2
);

  wire and_1_out, and_2_out, and_3_out, not_1_out, not_2_out, not_3_out;

  not not_1 (not_1_out, c3);
  not not_2 (not_2_out, c2);
  not not_3 (not_3_out, c0);
  and and_1 (and_1_out, not_1_out, not_2_out, c1, not_3_out);
  and and_2 (and_2_out, c3, c2, not_3_out);
  and and_3 (and_3_out, c3, c2, c1);
  or or_1 (HEX2, and_1_out, and_3_out, and_2_out);
endmodule

module M3 (
  input  c3,
  input  c2,
  input  c1,
  input  c0,
  output HEX3
);

  wire and_1_out, and_2_out, and_3_out, and_4_out, not_1_out, not_2_out, not_3_out, not_4_out;

  not not_1 (not_1_out, c2);
  not not_2 (not_2_out, c3);
  not not_3 (not_3_out, c1);
  not not_4 (not_4_out, c0);
  and and_1 (and_1_out, not_2_out, c2, not_3_out, not_4_out);
  and and_2 (and_2_out, not_1_out, not_3_out, c0);
  and and_3 (and_3_out, c2, c1, c0);
  and and_4 (and_4_out, c3, not_1_out, c1, not_4_out);
  or or_1 (HEX3, and_1_out, and_4_out, and_2_out, and_3_out);
endmodule

module M4 (
  input  c3,
  input  c2,
  input  c1,
  input  c0,
  output HEX4
);

  wire and_1_out, and_2_out, and_3_out, not_1_out, not_2_out, not_3_out;

  not not_1 (not_1_out, c2);
  not not_2 (not_2_out, c3);
  not not_3 (not_3_out, c1);
  and and_1 (and_1_out, not_2_out, c2, not_3_out);
  and and_2 (and_2_out, not_2_out, c0);
  and and_3 (and_3_out, not_1_out, not_3_out, c0);
  or or_1 (HEX4, and_1_out, and_2_out, and_3_out);
endmodule

module M5 (
  input  c3,
  input  c2,
  input  c1,
  input  c0,
  output HEX5
);

  wire and_1_out, and_2_out, and_3_out, and_4_out, not_1_out, not_2_out, not_3_out;

  not not_1 (not_1_out, c3);
  not not_2 (not_2_out, c2);
  not not_3 (not_3_out, c1);
  and and_1 (and_1_out, c3, c2, not_3_out, c0);
  and and_2 (and_2_out, not_1_out, not_2_out, c0);
  and and_3 (and_3_out, not_1_out, c1, c0);
  and and_4 (and_4_out, not_1_out, not_2_out, c1);
  or or_1 (HEX5, and_1_out, and_2_out, and_3_out, and_4_out);
endmodule

module M6 (
  input  c3,
  input  c2,
  input  c1,
  input  c0,
  output HEX6
);

  wire and_1_out, and_2_out, and_3_out, not_1_out, not_2_out, not_3_out, not_4_out;

  not not_1 (not_1_out, c3);
  not not_2 (not_2_out, c2);
  not not_3 (not_3_out, c1);
  not not_4 (not_4_out, c0);
  and and_1 (and_1_out, not_1_out, not_2_out, not_3_out);
  and and_2 (and_2_out, c3, c2, not_3_out, not_4_out);
  and and_3 (and_3_out, c0, c1, c2, not_1_out);
  or or_1 (HEX6, and_1_out, and_2_out, and_3_out);
endmodule

module max9 (
  input  clear,
  input  clk,
  input  enable,
  output [3:0] s
);

  wire and_1_out, not_1_out, not_2_out, not_3_out, or_1_out;

  not not_1 (not_1_out, enable);
  or or_1 (or_1_out, and_1_out, not_1_out);
  Counter #(.max('hf), .ongoal("stay"), .width(4)) counter_1 (
    .clr(clear), .load(or_1_out), .up(1'b1), .clk(clk), .D(4'b0000), .Q(s));  // open: count, carry
  not not_2 (not_2_out, s[1]);
  not not_3 (not_3_out, s[2]);
  and and_1 (and_1_out, s[0], not_2_out, not_3_out, s[3]);
endmodule

module experiment (
  input  clear,
  input  clk,
  input  enable,
  output [3:0] s
);

  wire and_1_out, not_1_out, or_1_out;

  not not_1 (not_1_out, enable);
  or or_1 (or_1_out, and_1_out, not_1_out);
  Counter #(.max('h9), .ongoal("load"), .width(4)) counter_1 (
    .clr(clear), .load(or_1_out), .up(1'b1), .clk(clk), .D(4'b0000), .Q(s));  // open: count, carry
  and and_1 (and_1_out, s[0], s[1], s[2], s[3]);
endmodule
