// Logisim project lab5_part3.circ as structural Verilog: 19 circuits, main circuit LUT
module mainmodule (
  input  KEY_0,
  input  [2:0] SW,
  input  key_1,
  output out_4,
  output out_5,
  output out_6,
  output out_7,
  output out_8,
  output out_9,
  output out_10,
  output out_11,
  output out_12,
  output out_13,
  output out_14,
  output out_15,
  output out_16,
  output out_17
);

  wire clock_1_out, ratedivider_1_newclk;
  wire [13:0] lut_1_s;

  Clock clock_1 (.out(clock_1_out));
  ratedivider ratedivider_1 (.clk(clock_1_out), .reset(KEY_0), .SW(2'b01), .newclk(ratedivider_1_newclk));
  LUT lut_1 (.SW(SW), .S(lut_1_s));
  rightshifter rightshifter_1 (
    .loadVal(lut_1_s), .load_n(key_1), .clk(ratedivider_1_newclk), .reset(KEY_0),
    .s({out_17, out_15, out_16, out_14, out_13, out_12, out_11, out_10, out_9, out_8, out_7, out_6, out_5, out_4}));
  LED led_1 (.in(out_4));
endmodule

module LUT (
  input  [2:0] SW,
  output [13:0] S
);

  Multiplexer #(.enable("false"), .select(3), .width(14)) multiplexer_1 (
    .in0(14'h2a00), .in1(14'h3800), .in2(14'h2b80), .in3(14'h2ae0), .in4(14'h2ee0), .in5(14'h3ab8),
    .in6(14'h3aee), .in7(14'h3ba8), .out(S), .sel(SW));
endmodule

module ratedivider (
  input  clk,
  input  reset,
  input  [1:0] SW,
  output newclk
);

  wire divideby8_1_counter_out, divideby32_1_counter_out, divideby64_1_counter_out;

  divideby8 divideby8_1 (.clear(reset), .clk(clk), .counter_out(divideby8_1_counter_out));
  divideby32 divideby32_1 (.clear(reset), .clk(clk), .counter_out(divideby32_1_counter_out));
  divideby64 divideby64_1 (.clear(reset), .clk(clk), .counter_out(divideby64_1_counter_out));
  Multiplexer #(.enable("false"), .select(2)) multiplexer_1 (
    .in0(clk), .in1(divideby8_1_counter_out), .in2(divideby32_1_counter_out), .in3(divideby64_1_counter_out),
    .out(newclk), .sel(SW));
endmodule

module divideby8 (
  input  clear,
  input  clk,
  output counter_out
);

  wire not_1_out, or_1_out;
  wire [2:0] counter_1_q;

  not not_1 (not_1_out, 1'b1);
  or or_1 (or_1_out, counter_out, not_1_out);
  Counter #(.max('h7), .ongoal("load"), .width(3)) counter_1 (
    .clr(clear), .load(or_1_out), .up(1'b1), .clk(clk), .D(3'b000), .Q(counter_1_q));  // open: count, carry
  and and_1 (counter_out, counter_1_q[0], counter_1_q[1], counter_1_q[2]);
endmodule

module divideBy2 (
  input  i,
  output s
);

  wire d_ff_1_qn;

  D_Flip_Flop d_ff_1 (.D(d_ff_1_qn), .clk(i), .Q(s), .Qn(d_ff_1_qn));  // open: preset, reset
endmodule

module displaycounter (
  input  clear,
  input  clk,
  input  enable,
  output [3:0] s
);

  wire and_1_out, not_1_out, or_1_out;

  not not_1 (not_1_out, enable);
  or or_1 (or_1_out, and_1_out, not_1_out);
  Counter #(.max('hf), .ongoal("load"), .width(4)) counter_1 (
    .clr(clear), .load(or_1_out), .up(1'b1), .clk(clk), .D(4'b0000), .Q(s));  // open: count, carry
  and and_1 (and_1_out, s[0], s[1], s[2], s[3]);
endmodule

module m_total (
  input  c3,
  input  c2,
  input  c1,
  input  c0,
  output HEX0,
  output HEX1,
  output HEX2,
  output HEX3,
  output HEX4,
  output HEX5,
  output HEX6
);

  M0 M0_1 (.c0(c0), .c1(c1), .c2(c2), .c3(c3), .HEX0(HEX0));
  M1 M1_1 (.c3(c3), .c2(c2), .c1(c1), .c0(c0), .HEX1(HEX1));
  M2 M2_1 (.c3(c3), .c2(c2), .c1(c1), .c0(c0), .HEX2(HEX2));
  M3 M3_1 (.c3(c3), .c2(c2), .c1(c1), .c0(c0), .HEX3(HEX3));
  M4 M4_1 (.c3(c3), .c2(c2), .c1(c1), .c0(c0), .HEX4(HEX4));
  M5 M5_1 (.c3(c3), .c2(c2), .c1(c1), .c0(c0), .HEX5(HEX5));
  M6 M6_1 (.c3(c3), .c2(c2), .c1(c1), .c0(c0), .HEX6(HEX6));
endmodule

module M0 (
  input  c0,
  input  c1,
  input  c2,
  input  c3,
  output HEX0
);

  wire and_1_out, and_2_out, and_3_out, and_4_out, not_1_out, not_2_out, not_3_out, not_4_out, not_5_out;

  not not_1 (not_1_out, c1);
  not not_2 (not_2_out, c2);
  not not_3 (not_3_out, c3);
  not not_4 (not_4_out, c0);
  and and_1 (and_1_out, not_4_out, not_1_out, c2, not_3_out);
  not not_5 (not_5_out, c2);
  and and_2 (and_2_out, not_3_out, not_5_out, not_1_out, c0);
  and and_3 (and_3_out, c0, not_1_out, c2, c3);
  and and_4 (and_4_out, c0, c1, not_2_out, c3);
  or or_1 (HEX0, and_1_out, and_2_out, and_3_out, and_4_out);
endmodule

module M1 (
  input  c3,
  input  c2,
  input  c1,
  input  c0,
  output HEX1
);

  wire and_1_out, and_2_out, and_3_out, and_4_out, not_1_out, not_2_out, not_3_out;

  not not_1 (not_1_out, c3);
  not not_2 (not_2_out, c1);
  not not_3 (not_3_out, c0);
  and and_1 (and_1_out, not_1_out, c2, not_2_out, c0);
  and and_2 (and_2_out, c3, c2, not_3_out);
  and and_3 (and_3_out, c3, c1, c0);
  and and_4 (and_4_out, c2, c1, not_3_out);
  or or_1 (HEX1, and_1_out, and_4_out, and_2_out, and_3_out);
endmodule

module M2 (
  input  c3,
  input  c2,
  input  c1,
  input  c0,
  output HEX2
);

  wire and_1_out, and_2_out, and_3_out, not_1_out, not_2_out, not_3_out;

  not not_1 (not_1_out, c3);
  not not_2 (not_2_out, c2);
  not not_3 (not_3_out, c0);
  and and_1 (and_1_out, not_1_out, not_2_out, c1, not_3_out);
  and and_2 (and_2_out, c3, c2, not_3_out);
  and and_3 (and_3_out, c3, c2, c1);
  or or_1 (HEX2, and_1_out, and_3_out, and_2_out);
endmodule

module M3 (
  input  c3,
  input  c2,
  input  c1,
  input  c0,
  output HEX3
);

  wire and_1_out, and_2_out, and_3_out, and_4_out, not_1_out, not_2_out, not_3_out, not_4_out;

  not not_1 (not_1_out, c2);
  not not_2 (not_2_out, c3);
  not not_3 (not_3_out, c1);
  not not_4 (not_4_out, c0);
  and and_1 (and_1_out, not_2_out, c2, not_3_out, not_4_out);
  and and_2 (and_2_out, not_1_out, not_3_out, c0);
  and and_3 (and_3_out, c2, c1, c0);
  and and_4 (and_4_out, c3, not_1_out, c1, not_4_out);
  or or_1 (HEX3, and_1_out, and_4_out, and_2_out, and_3_out);
endmodule

module M4 (
  input  c3,
  input  c2,
  input  c1,
  input  c0,
  output HEX4
);

  wire and_1_out, and_2_out, and_3_out, not_1_out, not_2_out, not_3_out;

  not not_1 (not_1_out, c2);
  not not_2 (not_2_out, c3);
  not not_3 (not_3_out, c1);
  and and_1 (and_1_out, not_2_out, c2, not_3_out);
  and and_2 (and_2_out, not_2_out, c0);
  and and_3 (and_3_out, not_1_out, not_3_out, c0);
  or or_1 (HEX4, and_1_out, and_2_out, and_3_out);
endmodule

module M5 (
  input  c3,
  input  c2,
  input  c1,
  input  c0,
  output HEX5
);

  wire and_1_out, and_2_out, and_3_out, and_4_out, not_1_out, not_2_out, not_3_out;

  not not_1 (not_1_out, c3);
  not not_2 (not_2_out, c2);
  not not_3 (not_3_out, c1);
  and and_1 (and_1_out, c3, c2, not_3_out, c0);
  and and_2 (and_2_out, not_1_out, not_2_out, c0);
  and and_3 (and_3_out, not_1_out, c1, c0);
  and and_4 (and_4_out, not_1_out, not_2_out, c1);
  or or_1 (HEX5, and_1_out, and_2_out, and_3_out, and_4_out);
endmodule

module M6 (
  input  c3,
  input  c2,
  input  c1,
  input  c0,
  output HEX6
);

  wire and_1_out, and_2_out, and_3_out, not_1_out, not_2_out, not_3_out, not_4_out;

  not not_1 (not_1_out, c3);
  not not_2 (not_2_out, c2);
  not not_3 (not_3_out, c1);
  not not_4 (not_4_out, c0);
  and and_1 (and_1_out, not_1_out, not_2_out, not_3_out);
  and and_2 (and_2_out, c3, c2, not_3_out, not_4_out);
  and and_3 (and_3_out, c0, c1, c2, not_1_out);
  or or_1 (HEX6, and_1_out, and_2_out, and_3_out);
endmodule

module divideby32 (
  input  clear,
  input  clk,
  output counter_out
);

  wire not_1_out, or_1_out;
  wire [4:0] counter_1_q;

  not not_1 (not_1_out, 1'b1);
  or or_1 (or_1_out, counter_out, not_1_out);
  Counter #(.max('h1f), .width(5)) counter_1 (
    .clr(clear), .load(or_1_out), .up(1'b1), .clk(clk), .D({5{1'b0}}), .Q(counter_1_q));  // open: count, carry
  and and_1 (counter_out, counter_1_q[0], counter_1_q[1], counter_1_q[2], counter_1_q[3], counter_1_q[4]);
endmodule

module divideby64 (
  input  clear,
  input  clk,
  output counter_out
);

  wire not_1_out, or_1_out;
  wire [5:0] counter_1_q;

  not not_1 (not_1_out, 1'b1);
  or or_1 (or_1_out, counter_out, not_1_out);
  Counter #(.max('h3f), .width(6)) counter_1 (
    .clr(clear), .load(or_1_out), .up(1'b1), .clk(clk), .D({6{1'b0}}), .Q(counter_1_q));  // open: count, carry
  and and_1 (counter_out, counter_1_q[0], counter_1_q[1], counter_1_q[2], counter_1_q[3], counter_1_q[4], counter_1_q[5]);
endmodule

module mux2 (
  input  x,
  input  y,
  input  s,
  output m
);

  Multiplexer #(.enable("false")) multiplexer_1 (.in0(x), .in1(y), .out(m), .sel(s));
endmodule

module Shifterbit (
  input  i,
  input  l_v,
  input  shift,
  input  l_n,
  input  clk,
  input  r,
  output s
);

  wire mux2_1_m, mux2_2_m;

  mux2 mux2_1 (.x(s), .y(i), .s(shift), .m(mux2_1_m));
  mux2 mux2_2 (.x(l_v), .y(mux2_1_m), .s(l_n), .m(mux2_2_m));
  D_Flip_Flop d_ff_1 (.D(mux2_2_m), .clk(clk), .Q(s), .reset(r));  // open: Qn, preset
endmodule

module rightshifter (
  input  [13:0] loadVal,
  input  load_n,
  input  clk,
  input  reset,
  output [13:0] s
);

  wire mux2_1_m;

  mux2 mux2_1 (.x(1'b0), .y(s[13]), .s(1'b0), .m(mux2_1_m));
  Shifterbit sb10 (.i(s[11]), .l_v(loadVal[10]), .shift(1'b1), .l_n(load_n), .clk(clk), .r(reset), .s(s[10]));
  Shifterbit sb11 (.i(s[12]), .l_v(loadVal[11]), .shift(1'b1), .l_n(load_n), .clk(clk), .r(reset), .s(s[11]));
  Shifterbit sb12 (.i(s[13]), .l_v(loadVal[12]), .shift(1'b1), .l_n(load_n), .clk(clk), .r(reset), .s(s[12]));
  Shifterbit sb13 (.i(mux2_1_m), .l_v(loadVal[13]), .shift(1'b1), .l_n(load_n), .clk(clk), .r(reset), .s(s[13]));
  Shifterbit sb0 (.i(s[1]), .l_v(loadVal[0]), .shift(1'b1), .l_n(load_n), .clk(clk), .r(reset), .s(s[0]));
  Shifterbit sb1 (.i(s[2]), .l_v(loadVal[1]), .shift(1'b1), .l_n(load_n), .clk(clk), .r(reset), .s(s[1]));
  Shifterbit sb2 (.i(s[3]), .l_v(loadVal[2]), .shift(1'b1), .l_n(load_n), .clk(clk), .r(reset), .s(s[2]));
  Shifterbit sb3 (.i(s[4]), .l_v(loadVal[3]), .shift(1'b1), .l_n(load_n), .clk(clk), .r(reset), .s(s[3]));
  Shifterbit sb4 (.i(s[5]), .l_v(loadVal[4]), .shift(1'b1), .l_n(load_n), .clk(clk), .r(reset), .s(s[4]));
  Shifterbit sb5 (.i(s[6]), .l_v(loadVal[5]), .shift(1'b1), .l_n(load_n), .clk(clk), .r(reset), .s(s[5]));
  Shifterbit sb6 (.i(s[7]), .l_v(loadVal[6]), .shift(1'b1), .l_n(load_n), .clk(clk), .r(reset), .s(s[6]));
  Shifterbit sb7 (.i(s[8]), .l_v(loadVal[7]), .shift(1'b1), .l_n(load_n), .clk(clk), .r(reset), .s(s[7]));
  Shifterbit sb8 (.i(s[9]), .l_v(loadVal[8]), .shift(1'b1), .l_n(load_n), .clk(clk), .r(reset), .s(s[8]));
  Shifterbit sb9 (.i(s[10]), .l_v(loadVal[9]), .shift(1'b1), .l_n(load_n), .clk(clk), .r(reset), .s(s[9]));
endmodule
