// Logisim project lab7_part2.circ as structural Verilog: 2 circuits, main circuit divideby16
module divideby16 (
  input  clear,
  input  clk,
  output counter_out
);

  wire not_1_out, or_1_out;
  wire [3:0] counter_1_q;

  not not_1 (not_1_out, 1'b1);
  or or_1 (or_1_out, counter_out, not_1_out);
  Counter #(.max('hf), .width(4)) counter_1 (
    .clr(clear), .load(or_1_out), .up(1'b1), .clk(clk), .D(4'b0000), .Q(counter_1_q));  // open: count, carry
  and and_1 (counter_out, counter_1_q[0], counter_1_q[1], counter_1_q[2], counter_1_q[3]);
endmodule

module main (
  input  [6:0] x,
  input  [6:0] y,
  input  in_3,
  input  in_4,
  input  [23:0] in_5
);

  wire clock_1_out, divideby16_1_counter_out;
  wire [3:0] adder_1_out, adder_2_out, register_1_q, register_2_q;
  wire [6:0] adder_3_out, adder_4_out, bit_extender_1_out, bit_extender_2_out;

  Adder #(.width(4)) adder_1 (.a(register_1_q), .b(4'b0001), .out(adder_1_out));  // open: cin, cout
  Clock clock_1 (.out(clock_1_out));
  Register #(.width(4)) register_1 (.D(adder_1_out), .en(1'b1), .clk(clock_1_out), .Q(register_1_q), .clr(in_4));
  Adder #(.width(4)) adder_2 (.a(register_2_q), .b(4'b0001), .out(adder_2_out));  // open: cin, cout
  Register #(.width(4)) register_2 (
    .D(adder_2_out), .en(divideby16_1_counter_out), .clk(clock_1_out), .Q(register_2_q), .clr(in_4));
  assign bit_extender_1_out = {{3{1'b0}}, register_1_q};  // Bit_Extender bit_extender_1
  assign bit_extender_2_out = {{3{1'b0}}, register_2_q};  // Bit_Extender bit_extender_2
  divideby16 divideby16_1 (.clear(in_4), .clk(clock_1_out), .counter_out(divideby16_1_counter_out));
  Adder #(.width(7)) adder_3 (.a(x), .b(bit_extender_1_out), .out(adder_3_out));  // open: cin, cout
  Adder #(.width(7)) adder_4 (.a(bit_extender_2_out), .b(y), .out(adder_4_out));  // open: cin, cout
  // RGB_Video #(.cursor("No Cursor")) rgb_video_1: pin names not known; wires that end beside it: in_4, clock_1_out, in_3, adder_3_out, adder_4_out, in_5
endmodule
