// Logisim project lab7_part3.circ as structural Verilog: 7 circuits, main circuit divideby16
module main (
  input  [6:0] x,
  input  [6:0] y,
  input  reset,
  input  in_4,
  input  enable,
  input  [23:0] colour
);

  wire clock_1_out, divideby256_1_counter_out, multiplexer_1_out;
  wire [6:0] datapath_1_x_output, datapath_1_y_output;

  Clock clock_1 (.out(clock_1_out));
  datapath datapath_1 (
    .x(x), .y(y), .clk(clock_1_out), .reset(reset), .x_output(datapath_1_x_output),
    .y_output(datapath_1_y_output));
  divideby256 divideby256_1 (.clear(reset), .clk(clock_1_out), .counter_out(divideby256_1_counter_out));
  Multiplexer #(.enable("false")) multiplexer_1 (
    .in0(reset), .in1(divideby256_1_counter_out), .out(multiplexer_1_out), .sel(in_4));
  // RGB_Video #(.cursor("No Cursor")) rgb_video_1: pin names not known; wires that end beside it: multiplexer_1_out, clock_1_out, enable, datapath_1_x_output, datapath_1_y_output, colour
endmodule

module divideby16 (
  input  clear,
  input  clk,
  output counter_out
);

  wire not_1_out, or_1_out;
  wire [3:0] counter_1_q;

  not not_1 (not_1_out, 1'b1);
  or or_1 (or_1_out, counter_out, not_1_out);
  Counter #(.max('hf), .width(4)) counter_1 (
    .clr(clear), .load(or_1_out), .up(1'b1), .clk(clk), .D(4'b0000), .Q(counter_1_q));  // open: count, carry
  and and_1 (counter_out, counter_1_q[0], counter_1_q[1], counter_1_q[2], counter_1_q[3]);
endmodule

module divideby256 (
  input  clear,
  input  clk,
  output counter_out
);

  wire not_1_out, or_1_out;
  wire [7:0] counter_1_q;

  not not_1 (not_1_out, 1'b1);
  or or_1 (or_1_out, counter_out, not_1_out);
  Counter counter_1 (
    .clr(clear), .load(or_1_out), .up(1'b1), .clk(clk), .D({8{1'b0}}), .Q(counter_1_q));  // open: count, carry
  and and_1 (counter_out, counter_1_q[0], counter_1_q[1], counter_1_q[2], counter_1_q[3], counter_1_q[4], counter_1_q[5], counter_1_q[6], counter_1_q[7]);
endmodule

module changexy (
  input  [6:0] x,
  input  [6:0] y,
  input  [1:0] ori_dir,
  output [6:0] next_x,
  output [1:0] next_dir,
  output [6:0] next_y
);

  wire adder_2_cout, adder_4_cout, and_1_out, and_2_out, and_3_out, and_4_out, not_1_out, not_2_out,
       not_3_out, not_4_out, or_1_out, or_2_out, subtractor_1_bout, subtractor_2_bout;
  wire [6:0] adder_1_out, adder_3_out, multiplexer_1_out, multiplexer_2_out, multiplexer_3_out,
       multiplexer_4_out, subtractor_1_out, subtractor_2_out;

  Subtractor #(.width(7)) subtractor_1 (
    .a(x), .b(7'b0010000), .out(subtractor_1_out), .bout(subtractor_1_bout));  // open: bin
  Adder #(.width(7)) adder_1 (.a(7'b0010000), .b(x), .out(adder_1_out));  // open: cin, cout
  Adder #(.width(7)) adder_2 (.a(x), .b(7'b0100000), .cout(adder_2_cout));  // open: out, cin
  Adder #(.width(7)) adder_3 (.a(y), .b(7'b0010000), .out(adder_3_out));  // open: cin, cout
  Subtractor #(.width(7)) subtractor_2 (
    .a(y), .b(7'b0010000), .out(subtractor_2_out), .bout(subtractor_2_bout));  // open: bin
  Adder #(.width(7)) adder_4 (.a(y), .b(7'b0100000), .cout(adder_4_cout));  // open: out, cin
  Multiplexer #(.enable("false"), .width(7)) multiplexer_1 (
    .in0(adder_3_out), .in1(subtractor_2_out), .out(multiplexer_1_out), .sel(adder_4_cout));
  Multiplexer #(.enable("false"), .width(7)) multiplexer_2 (
    .in0(subtractor_2_out), .in1(adder_3_out), .out(multiplexer_2_out), .sel(subtractor_2_bout));
  not not_1 (not_1_out, ori_dir[0]);
  Multiplexer #(.enable("false"), .width(7)) multiplexer_3 (
    .in0(adder_1_out), .in1(subtractor_1_out), .out(multiplexer_3_out), .sel(adder_2_cout));
  Multiplexer #(.enable("false"), .width(7)) multiplexer_4 (
    .in0(subtractor_1_out), .in1(adder_1_out), .out(multiplexer_4_out), .sel(subtractor_1_bout));
  and and_1 (and_1_out, ori_dir[0], adder_2_cout);
  and and_2 (and_2_out, not_1_out, subtractor_1_bout);
  Multiplexer #(.enable("false"), .width(7)) multiplexer_5 (
    .in0(multiplexer_1_out), .in1(multiplexer_2_out), .out(next_y), .sel(ori_dir[1]));
  not not_2 (not_2_out, ori_dir[1]);
  Multiplexer #(.enable("false"), .width(7)) multiplexer_6 (
    .in0(multiplexer_4_out), .in1(multiplexer_3_out), .out(next_x), .sel(ori_dir[0]));
  and and_3 (and_3_out, ori_dir[1], subtractor_2_bout);
  and and_4 (and_4_out, not_2_out, adder_4_cout);
  or or_1 (or_1_out, and_1_out, and_2_out);
  or or_2 (or_2_out, and_3_out, and_4_out);
  Multiplexer #(.enable("false")) multiplexer_7 (.in0(ori_dir[0]), .in1(not_3_out), .out(next_dir[0]), .sel(or_1_out));
  not not_3 (not_3_out, ori_dir[0]);
  Multiplexer #(.enable("false")) multiplexer_8 (.in0(ori_dir[1]), .in1(not_4_out), .out(next_dir[1]), .sel(or_2_out));
  not not_4 (not_4_out, ori_dir[1]);
endmodule

module datapath (
  input  [6:0] x,
  input  [6:0] y,
  input  clk,
  input  reset,
  output [6:0] x_output,
  output [6:0] y_output
);

  wire divideby256_1_counter_out, keepatone_1_out_3, multiplexer_1_out;
  wire [1:0] changexy_1_next_dir, register_3_q;
  wire [6:0] changexy_1_next_x, changexy_1_next_y, multiplexer_2_out, multiplexer_3_out, register_1_q,
       register_2_q;

  Multiplexer #(.enable("false")) multiplexer_1 (
    .in0(1'b1), .in1(divideby256_1_counter_out), .out(multiplexer_1_out), .sel(keepatone_1_out_3));
  keepatone keepatone_1 (.clear(reset), .clk(clk), .out_3(keepatone_1_out_3));
  Multiplexer #(.enable("false"), .width(7)) multiplexer_2 (
    .in0(x), .in1(changexy_1_next_x), .out(multiplexer_2_out), .sel(keepatone_1_out_3));
  Multiplexer #(.enable("false"), .width(7)) multiplexer_3 (
    .in0(y), .in1(changexy_1_next_y), .out(multiplexer_3_out), .sel(keepatone_1_out_3));
  Register #(.width(7)) register_1 (
    .D(multiplexer_2_out), .en(multiplexer_1_out), .clk(clk), .Q(register_1_q), .clr(reset));
  Register #(.width(7)) register_2 (
    .D(multiplexer_3_out), .en(multiplexer_1_out), .clk(clk), .Q(register_2_q), .clr(reset));
  divideby256 divideby256_1 (.clear(reset), .clk(clk), .counter_out(divideby256_1_counter_out));
  Register #(.width(2)) register_3 (
    .D(changexy_1_next_dir), .en(1'b1), .clk(divideby256_1_counter_out), .Q(register_3_q), .clr(reset));
  submain submain_1 (.x(register_1_q), .clk(clk), .y(register_2_q), .reset(reset), .x_out(x_output), .y_out(y_output));
  changexy changexy_1 (
    .x(register_1_q), .y(register_2_q), .ori_dir(register_3_q), .next_x(changexy_1_next_x),
    .next_dir(changexy_1_next_dir), .next_y(changexy_1_next_y));
endmodule

module keepatone (
  input  clear,
  input  clk,
  output out_3
);

  wire and_1_out, not_1_out, or_1_out;
  wire [0:0] counter_1_q;

  not not_1 (not_1_out, 1'b1);
  or or_1 (or_1_out, and_1_out, not_1_out);
  Counter #(.max('h2), .ongoal("stay"), .width(2)) counter_1 (
    .clr(clear), .load(or_1_out), .up(1'b1), .clk(clk), .D(2'b00), .Q({out_3, counter_1_q[0]}));  // open: count, carry
  and and_1 (and_1_out, counter_1_q[0], out_3);
endmodule

module submain (
  input  [6:0] x,
  input  clk,
  input  [6:0] y,
  input  reset,
  output [6:0] x_out,
  output [6:0] y_out
);

  wire divideby16_1_counter_out;
  wire [3:0] adder_1_out, adder_2_out, register_1_q, register_2_q;
  wire [6:0] bit_extender_1_out, bit_extender_2_out;

  Adder #(.width(4)) adder_1 (.a(register_1_q), .b(4'b0001), .out(adder_1_out));  // open: cin, cout
  Register #(.width(4)) register_1 (.D(adder_1_out), .en(1'b1), .clk(clk), .Q(register_1_q), .clr(reset));
  Adder #(.width(4)) adder_2 (.a(register_2_q), .b(4'b0001), .out(adder_2_out));  // open: cin, cout
  Register #(.width(4)) register_2 (
    .D(adder_2_out), .en(divideby16_1_counter_out), .clk(clk), .Q(register_2_q), .clr(reset));
  assign bit_extender_1_out = {{3{1'b0}}, register_1_q};  // Bit_Extender bit_extender_1
  assign bit_extender_2_out = {{3{1'b0}}, register_2_q};  // Bit_Extender bit_extender_2
  divideby16 divideby16_1 (.clear(reset), .clk(clk), .counter_out(divideby16_1_counter_out));
  Adder #(.width(7)) adder_3 (.a(x), .b(bit_extender_1_out), .out(x_out));  // open: cin, cout
  Adder #(.width(7)) adder_4 (.a(bit_extender_2_out), .b(y), .out(y_out));  // open: cin, cout
endmodule
